# Fritzing sketch Week1_TrafficLight (saved by Fritzing 0.9.3b)
breadboards: 1

parts:
  LED1 = LED - 5mm [color="Red (633nm)" package="5 mm [THT]"]
  LED2 = LED - 5mm [color="Yellow (595nm)" package="5 mm [THT]"]
  LED3 = LED - 5mm [color="Green (555nm)" package="5 mm [THT]"]
  R2 = Resistor [tolerance=±5% resistance=220 package=THT]
  R3 = Resistor [tolerance=±5% resistance=220 package=THT]
  R4 = Resistor [tolerance=±5% resistance=220 package=THT]
  Part1 = Arduino Uno (Rev3)

nets:
  N1: LED1.cathode, R2.Pin_1
  N2: LED1.anode, Part1.D8
  N3: LED2.cathode, R3.Pin_1
  N4: LED2.anode, Part1.D10_PWM/SS
  N5: LED3.cathode, R4.Pin_1
  N6: LED3.anode, Part1.D12/MISO
  N7: R2.Pin_0, R3.Pin_0, R4.Pin_0, Part1.GND

// code stored in the sketch: Untitled2.ino

